# Fritzing sketch esp8266_bl999 (saved by Fritzing 0.9.2b)
circuit board: 8.46667cm x 5.64444cm
breadboards: 1

parts:
  U2 = RF-LINK_RX [package=rf-link_rx]
  LED1 = LED - 3mm [color="Red (633nm)" package="3 mm [THT]"]
  LED2 = LED - 3mm [color="Red (633nm)" package="3 mm [THT]"]
  LED3 = LED - 3mm [color="Red (633nm)" package="3 mm [THT]"]
  R1 = Resistor [tolerance=±5% resistance=220 package=THT]
  R2 = Resistor [tolerance=±5% resistance=220 package=THT]
  R3 = Resistor [tolerance=±5% resistance=220 package=THT]
  S1 = Momentary Switch [package=ksa_sealed_tac_switch]
  R4 = Resistor [tolerance=±5% resistance=220 package=THT]
  U1 = ESP8266 WiFi Module [part_number=ESP8266]
  R5 = Resistor [tolerance=±5% resistance=220 package=THT]
  R6 = Resistor [tolerance=±5% resistance=220 package=THT]
  S2 = Momentary Switch [package=ksa_sealed_tac_switch]
  VCC1 = 4 x AAA Battery Mount
  U3 = V_REG_LD1117VXX [package=78xxl]

nets:
  GND: U2.GND, LED1.cathode, LED2.cathode, LED3.cathode, S1.3, S1.4, U1.GND, S2.1, S2.2, VCC1.-, U3.GND
  N1: U2.+5V, VCC1.+, U3.IN
  N2: LED1.anode, R3.Pin_0
  N3: LED2.anode, R2.Pin_0
  N4: LED3.anode, R1.Pin_0
  N5: S1.1, S1.2, R4.Pin_0
  N6: R4.Pin_1, U1.VCC, R5.Pin_1, R6.Pin_0, U3.OUT
  N7: U1.GPIO_0, R6.Pin_1, S2.3, S2.4
  N8: U1.CH_PD, R5.Pin_0
